// Logisim project 5票选择.circ as structural Verilog: 1 circuit, main circuit main
module main (
  input  g,
  input  s,
  input  [1:0] I4_I3,
  input  [2:0] I2_I1_I0,
  output led
);

  wire decoder_1_out0, decoder_1_out1, decoder_1_out2, decoder_1_out3, decoder_2_p5, decoder_3_out3,
       decoder_3_out5, decoder_3_out6, decoder_3_out7, decoder_4_out3, decoder_4_out5, decoder_4_out6,
       decoder_4_out7, decoder_5_out1, decoder_5_out2, decoder_5_out3, decoder_5_out4, decoder_5_out5,
       decoder_5_out6, decoder_5_out7;

  Decoder #(.select(2), .tristate("false"), .disabled("Z"), .enable("false")) decoder_1 (
    .out0(decoder_1_out0), .out1(decoder_1_out1), .out2(decoder_1_out2), .out3(decoder_1_out3), .sel(I4_I3));
  // Decoder #(.select(3), .tristate("false"), .disabled("Z"), .enable("false")) decoder_2: pin names not known; wires that end beside it: g, s, decoder_1_out0, I2_I1_I0, decoder_2_p5
  Decoder #(.select(3), .tristate("false"), .disabled("Z"), .enable("false")) decoder_3 (
    .out3(decoder_3_out3), .out5(decoder_3_out5), .out6(decoder_3_out6), .out7(decoder_3_out7), .sel(I2_I1_I0));  // open: out0, out1, out2, out4
  Decoder #(.select(3), .tristate("false"), .disabled("Z"), .enable("false")) decoder_4 (
    .out3(decoder_4_out3), .out5(decoder_4_out5), .out6(decoder_4_out6), .out7(decoder_4_out7), .sel(I2_I1_I0));  // open: out0, out1, out2, out4
  Decoder #(.select(3), .tristate("false"), .disabled("Z"), .enable("false")) decoder_5 (
    .out1(decoder_5_out1), .out2(decoder_5_out2), .out3(decoder_5_out3), .out4(decoder_5_out4),
    .out5(decoder_5_out5), .out6(decoder_5_out6), .out7(decoder_5_out7), .sel(I2_I1_I0));  // open: out0
  nand nand_1 (led, decoder_2_p5, decoder_3_out3, decoder_3_out5, decoder_3_out6, decoder_3_out7, decoder_4_out3, decoder_4_out5, decoder_4_out6, decoder_4_out7, decoder_5_out1, decoder_5_out2, decoder_5_out3, decoder_5_out4, decoder_5_out5, decoder_5_out6, decoder_5_out7);

  // Notes on the sheet:
  //   74LS139
  //   74LS138
  //   74LS138
  //   74LS138
  //   74LS138
endmodule
